# Fritzing sketch RPI (saved by Fritzing 0.8.3b)
circuit board: 6.80157cm x 4.47792cm

parts:
  PlotterPi = Raspberry Pi rev2
  Power_plug1 = Power plug
  C1 = Ceramic Capacitor [capacitance=0.1µF voltage=16V part_number=0.33uF package="100 mil [THT, multilayer]"]
  C2 = Ceramic Capacitor [capacitance=0.1µF voltage=16V package="100 mil [THT, multilayer]"]
  M1 = Stepper Motor - Bipolar
  J1 = single row smd female pin header, 8 pins [form="♀ (female)"]
  J2 = single row smd female pin header, 8 pins [form="♀ (female)"]
  R1 = Resistor [tolerance=±5% resistance=1 part_number=??? package=THT]
  C3 = Electrolytic Capacitor [capacitance=1µF voltage=16V part_number=100uF package="100 mil [THT, electrolytic]"]
  IC1 = Voltage Regulator [package=to220-igo]
  J3 = Basic Servo
  J5 = single row smd female pin header, 8 pins [form="♀ (female)"]
  R2 = Resistor [tolerance=±5% resistance=1 part_number=??? package=THT]
  M2 = Stepper Motor - Bipolar
  J4 = single row smd female pin header, 8 pins [form="♀ (female)"]

nets:
  3V3: PlotterPi.3V3, C2.0, IC1.OUT, J3.vcc
  GND: PlotterPi.GIPO_3, Power_plug1.GND, C1.0, C2.1, J2.pin2, C3.-, IC1.GND, J3.gnd, J5.pin2
  N1: PlotterPi.GPIO_23, J1.pin7
  N2: PlotterPi.GPIO_17, J1.pin8
  N3: PlotterPi.GPIO_18, J3.pulse
  N4: PlotterPi.GPIO4, J4.pin7
  N5: PlotterPi.GPIO_24, J4.pin8
  N6: Power_plug1.VCC, C1.1, J2.pin1, C3.+, IC1.IN, J5.pin1
  N7: M1.A, J2.pin3
  N8: M1.C, J2.pin4
  N9: M1.B, J2.pin5
  N10: M1.D, J2.pin6
  N11: J1.pin2, R1.Pin_0
  N12: J1.pin3, J2.pin7
  N13: J1.pin5, J1.pin6
  N14: J2.pin8, R1.Pin_1
  N15: J5.pin3, M2.A
  N16: J5.pin4, M2.C
  N17: J5.pin5, M2.B
  N18: J5.pin6, M2.D
  N19: J5.pin7, J4.pin3
  N20: J5.pin8, R2.Pin_1
  N21: R2.Pin_0, J4.pin2
  N22: J4.pin5, J4.pin6

notes:
  ENABLE
  MS1
  MS2
  MS3
  RESET
  SLEEP
  STEP
  DIR
  VMOT
  GND
  2B
  2A
  1A
  1B
  VDD
