# Fritzing sketch vPlotter (saved by Fritzing 0.8.5b)
circuit board: 4cm x 5cm

parts:
  Power = Power plug
  M1 = Stepper Motor - Bipolar
  R1 = Resistor [tolerance=±5% resistance=100k package=THT]
  C3 = Electrolytic Capacitor [capacitance=1µF voltage=16V part_number=100uF package="100 mil [THT, electrolytic]"]
  R2 = Resistor [tolerance=±5% resistance=100k package=THT]
  M2 = Stepper Motor - Bipolar
  4 = female pin header, 1 pin [form="♀ (female)" part_number=4]
  gnd = female pin header, 1 pin [form="♀ (female)" part_number=gnd]
  3v = female pin header, 1 pin [form="♀ (female)" part_number=3v]
  J4 = female pin header, 8 pins [form="♀ (female)"]
  J5 = female pin header, 8 pins [form="♀ (female)"]
  J2 = female pin header, 8 pins [form="♀ (female)"]
  J1 = female pin header, 8 pins [form="♀ (female)"]
  Servo = Basic Servo
  gnd_2 = female pin header, 1 pin [form="♀ (female)" part_number=gnd]
  18/17 = female pin header, 2 pins [form="♀ (female)" part_number=17/18]
  Raspberry_Pi_rev1 = Raspberry Pi B rev2  # not connected
  22/23 = female pin header, 2 pins [form="♀ (female)" part_number=23/24]

nets:
  N1: Power.GND, C3.-, J5.pin2, J2.pin2
  N2: Power.VCC, C3.+, J5.pin1, J2.pin1
  N3: M1.A, J2.pin3
  N4: M1.C, J2.pin4
  N5: M1.B, J2.pin5
  N6: M1.D, J2.pin6
  N7: R1.Pin_0, J1.pin2
  N8: R1.Pin_1, gnd.pin1, J2.pin8, Servo.gnd
  N9: R2.Pin_0, J4.pin2
  N10: R2.Pin_1, J5.pin8, gnd_2.pin1
  N11: M2.A, J5.pin3
  N12: M2.C, J5.pin4
  N13: M2.B, J5.pin5
  N14: M2.D, J5.pin6
  N15: 4.pin1, J1.pin8
  N16: 3v.pin1, J4.pin3, J5.pin7, J2.pin7, J1.pin3, Servo.vcc
  N17: J4.pin5, J4.pin6
  N18: J4.pin7, 22/23.pin1
  N19: J4.pin8, 22/23.pin2
  N20: J1.pin5, J1.pin6
  N21: J1.pin7, 18/17.pin2
  N22: Servo.pulse, 18/17.pin1

notes:
  ENABLE
  MS1
  MS2
  MS3
  RESET
  SLEEP
  STEP
  DIR
  VMOT
  GND
  2B
  2A
  1A
  1B
  VDD
